// Logisim project L0.Q1.CRC.circ as structural Verilog: 3 circuits, main circuit CRC
module CRC (
  input  [7:0] in_1,
  input  [3:0] in_2,
  output [10:0] out_3
);

  wire [2:0] move_right_1_out_3, move_right_2_out_3, move_right_3_out_3, move_right_4_out_3,
       move_right_5_out_3, move_right_7_out_3;
  wire [3:1] move_right_6_out_3;

  move_right move_right_1 (.in_1(in_1[7:4]), .in_2(in_2), .out_3(move_right_1_out_3));
  move_right move_right_2 (.in_1({move_right_1_out_3, in_1[3]}), .in_2(in_2), .out_3(move_right_2_out_3));
  move_right move_right_3 (.in_1({move_right_2_out_3, in_1[2]}), .in_2(in_2), .out_3(move_right_3_out_3));
  move_right move_right_4 (.in_1({move_right_3_out_3, in_1[1]}), .in_2(in_2), .out_3(move_right_4_out_3));
  move_right move_right_5 (.in_1({move_right_4_out_3, in_1[0]}), .in_2(in_2), .out_3(move_right_5_out_3));
  move_right move_right_6 (.in_1({move_right_5_out_3, 1'b0}), .in_2(in_2), .out_3(move_right_6_out_3));
  move_right move_right_7 (.in_1({move_right_6_out_3, 1'b0}), .in_2(in_2), .out_3(move_right_7_out_3));
  move_right move_right_8 (.in_1({move_right_7_out_3, 1'b0}), .in_2(in_2), .out_3(out_3[2:0]));

  assign out_3[10:3] = in_1;

  // Other names for the same wires on the sheet: DVDR[3:0] = in_2; OUT[2:0] = out_3[2:0]
endmodule

module CRC4bits (
  input  [3:0] divided,
  input  [3:0] divider,
  output [2:0] out_3
);

  xor xor_1 (out_3[0], divided[0], divider[0]);
  xor xor_2 (out_3[1], divided[1], divider[1]);
  xor xor_3 (out_3[2], divided[2], divider[2]);
endmodule

module move_right (
  input  [3:0] in_1,
  input  [3:0] in_2,
  output [2:0] out_3
);

  wire [2:0] crc4bits_1_out_3;

  CRC4bits crc4bits_1 (.divided(in_1), .divider(in_2), .out_3(crc4bits_1_out_3));
  Multiplexer #(.width(3)) multiplexer_1 (
    .in0(in_1[2:0]), .in1(crc4bits_1_out_3), .out(out_3), .sel(in_1[3]));  // open: en
endmodule
