// Logisim project L0.Q4.FSM.circ as structural Verilog: 2 circuits, main circuit fsm
module fsm (
  input  in_1,
  input  [1:0] in_2,
  output out_3
);

  wire and_1_out, and_2_out, clock_1_out, logic_1_ns0, logic_1_ns1, not_1_out, not_2_out, register_1_q,
       register_2_q;

  \logic  logic_1 (
    .S1(register_1_q), .S0(register_2_q), .I1(in_2[1]), .I0(in_2[0]), .NS1(logic_1_ns1), .NS0(logic_1_ns0),
    .OUT(out_3));
  not not_1 (not_1_out, in_1);
  Clock clock_1 (.out(clock_1_out));
  not not_2 (not_2_out, in_1);
  and and_1 (and_1_out, not_1_out, logic_1_ns1);
  and and_2 (and_2_out, logic_1_ns0, not_2_out);
  Register #(.width(1)) register_1 (.D(and_1_out), .Q(register_1_q), .clk(clock_1_out));  // open: en, clr
  Register #(.width(1)) register_2 (.D(and_2_out), .Q(register_2_q), .clk(clock_1_out));  // open: en, clr

  // Other names for the same wires on the sheet: RST = in_1
endmodule

module \logic  (
  input  S1,
  input  S0,
  input  I1,
  input  I0,
  output NS1,
  output NS0,
  output OUT
);

  wire not_1_out, not_2_out, not_3_out;

  and and_1 (NS1, S0, not_1_out);
  not not_1 (not_1_out, I0);
  not not_2 (not_2_out, I1);
  and and_2 (NS0, not_2_out, I0);
  and and_3 (OUT, S1, not_3_out);
  not not_3 (not_3_out, I0);
endmodule
