// Logisim project cpu.circ as structural Verilog: 7 circuits, main circuit main
module main (
  input  Reset,
  output [31:0] Instr,
  output RegWrite,
  output [4:0] RegAddr,
  output [31:0] RegData,
  output MemWrite,
  output [4:0] MemAddr,
  output [31:0] MemData
);

  wire ALUsrc, clk, GRF_WD, GRF_WS, nPC_sel, zero;
  wire [1:0] ALUctr, EXTctr;
  wire [31:0] alu_1_aluout, dm_1_data_r, ext_1_out_3, grf_1_out_8, multiplexer_2_out;

  Clock clock_1 (.out(clk));
  IFU ifu_1 (.offset(Instr[15:0]), .nPC_sel(nPC_sel), .zero(zero), .clock(clk), .reset(Reset), .Instr(Instr));
  Controller controller_1 (
    .opcode(Instr[31:26]), .func(Instr[5:0]), .nPC_sel(nPC_sel), .GRF_WE(RegWrite), .DM_WE(MemWrite),
    .GRF_WD(GRF_WD), .ALUsrc(ALUsrc), .GRF_WS(GRF_WS), .ALUctr(ALUctr), .EXTctr(EXTctr));
  Multiplexer #(.width(5)) multiplexer_1 (
    .in0(Instr[20:16]), .in1(Instr[15:11]), .out(RegAddr), .sel(GRF_WD));  // open: en
  GRF grf_1 (
    .clk(clk), .reset(Reset), .WE(RegWrite), .RS(Instr[25:21]), .RT(Instr[20:16]), .RD(RegAddr),
    .WD(RegData), .out_8(grf_1_out_8), .out_9(MemData));
  EXT ext_1 (.in_1(Instr[15:0]), .in_2(EXTctr), .out_3(ext_1_out_3));
  Multiplexer #(.width(32)) multiplexer_2 (
    .in0(MemData), .in1(ext_1_out_3), .out(multiplexer_2_out), .sel(ALUsrc));  // open: en
  ALU alu_1 (
    .opA(grf_1_out_8), .opB(multiplexer_2_out), .ALUctr(ALUctr),
    .ALUout({alu_1_aluout[31:7], MemAddr, alu_1_aluout[1:0]}), .zero(zero));
  DM dm_1 (.Addr(MemAddr), .data_w(MemData), .write_en(MemWrite), .clk(clk), .reset(Reset), .data_r(dm_1_data_r));
  Multiplexer #(.width(32)) multiplexer_3 (
    .in0({alu_1_aluout[31:7], MemAddr, alu_1_aluout[1:0]}), .in1(dm_1_data_r), .out(RegData), .sel(GRF_WS));  // open: en

  // Other names for the same wires on the sheet: DM_WD[31:0] = MemData; DM_WE = MemWrite; GRF_WE = RegWrite;
  //   imm[15:0] = Instr[15:0]; toGRF[31:0] = RegData
endmodule

module IFU (
  input  [15:0] offset,
  input  nPC_sel,
  input  zero,
  input  clock,
  input  reset,
  output [31:0] Instr
);

  wire and_1_out;
  wire [31:0] adder_1_out, adder_2_out, bit_extender_1_out, multiplexer_1_out, PC;

  Adder #(.width(32)) adder_1 (.a(PC), .b(32'h4), .out(adder_1_out));  // open: cin, cout
  and and_1 (and_1_out, nPC_sel, zero);
  assign bit_extender_1_out = {{14{offset[15]}}, {offset, 2'b00}};  // Bit_Extender bit_extender_1
  Adder #(.width(32)) adder_2 (.a(adder_1_out), .b(bit_extender_1_out), .out(adder_2_out));  // open: cin, cout
  Multiplexer #(.width(32)) multiplexer_1 (
    .in0(adder_1_out), .in1(adder_2_out), .out(multiplexer_1_out), .sel(and_1_out));  // open: en
  Register #(.width(32)) u_PC (.D(multiplexer_1_out), .Q(PC), .clk(clock), .clr(reset));  // open: en
  ROM #(.addrWidth(5), .dataWidth(32)) rom_1 (.addr(PC[6:2]), .data(Instr));  // open: sel

  // Notes on the sheet:
  //   contents of rom_1 (hex, n*v repeats v):
  //   34011234 211021 3c032478 34032478 622023 ac810000 8c850000 10250003 0 0 34064321 34012345 3c002333
  //   ac810004
endmodule

module GRF (
  input  clk,
  input  reset,
  input  WE,
  input  [4:0] RS,
  input  [4:0] RT,
  input  [4:0] RD,
  input  [31:0] WD,
  output [31:0] out_8,
  output [31:0] out_9
);

  wire demultiplexer_1_out0, demultiplexer_1_out1, demultiplexer_1_out2, demultiplexer_1_out3,
       demultiplexer_1_out4, demultiplexer_1_out5, demultiplexer_1_out6, demultiplexer_1_out7,
       demultiplexer_1_out8, demultiplexer_1_out9, demultiplexer_1_out10, demultiplexer_1_out11,
       demultiplexer_1_out12, demultiplexer_1_out13, demultiplexer_1_out14, demultiplexer_1_out15,
       demultiplexer_1_out16, demultiplexer_1_out17, demultiplexer_1_out18, demultiplexer_1_out19,
       demultiplexer_1_out20, demultiplexer_1_out21, demultiplexer_1_out22, demultiplexer_1_out23,
       demultiplexer_1_out24, demultiplexer_1_out25, demultiplexer_1_out26, demultiplexer_1_out27,
       demultiplexer_1_out28, demultiplexer_1_out29, demultiplexer_1_out30, demultiplexer_1_out31;
  wire [31:0] register_1_q, register_2_q, register_3_q, register_4_q, register_5_q, register_6_q,
       register_7_q, register_8_q, register_9_q, register_10_q, register_11_q, register_12_q, register_13_q,
       register_14_q, register_15_q, register_16_q, register_17_q, register_18_q, register_19_q,
       register_20_q, register_21_q, register_22_q, register_23_q, register_24_q, register_25_q,
       register_26_q, register_27_q, register_28_q, register_29_q, register_30_q, register_31_q,
       register_32_q;

  Register #(.width(32)) register_1 (.D(WD), .en(demultiplexer_1_out0), .Q(register_1_q), .clk(clk), .clr(1'b1));
  Register #(.width(32)) register_2 (.D(WD), .en(demultiplexer_1_out1), .Q(register_2_q), .clk(clk), .clr(reset));
  Register #(.width(32)) register_3 (.D(WD), .en(demultiplexer_1_out2), .Q(register_3_q), .clk(clk), .clr(reset));
  Register #(.width(32)) register_4 (.D(WD), .en(demultiplexer_1_out3), .Q(register_4_q), .clk(clk), .clr(reset));
  Register #(.width(32)) register_5 (.D(WD), .en(demultiplexer_1_out4), .Q(register_5_q), .clk(clk), .clr(reset));
  Register #(.width(32)) register_6 (.D(WD), .en(demultiplexer_1_out5), .Q(register_6_q), .clk(clk), .clr(reset));
  Register #(.width(32)) register_7 (.D(WD), .en(demultiplexer_1_out6), .Q(register_7_q), .clk(clk), .clr(reset));
  Register #(.width(32)) register_8 (.D(WD), .en(demultiplexer_1_out7), .Q(register_8_q), .clk(clk), .clr(reset));
  Register #(.width(32)) register_9 (.D(WD), .en(demultiplexer_1_out8), .Q(register_9_q), .clk(clk), .clr(reset));
  Register #(.width(32)) register_10 (.D(WD), .en(demultiplexer_1_out9), .Q(register_10_q), .clk(clk), .clr(reset));
  Register #(.width(32)) register_11 (.D(WD), .en(demultiplexer_1_out10), .Q(register_11_q), .clk(clk), .clr(reset));
  Register #(.width(32)) register_12 (.D(WD), .en(demultiplexer_1_out11), .Q(register_12_q), .clk(clk), .clr(reset));
  Multiplexer #(.select(5), .width(32)) multiplexer_1 (
    .in0(register_1_q), .in1(register_2_q), .in2(register_3_q), .in3(register_4_q), .in4(register_5_q),
    .in5(register_6_q), .in6(register_7_q), .in7(register_8_q), .in8(register_9_q), .in9(register_10_q),
    .in10(register_11_q), .in11(register_12_q), .in12(register_16_q), .in13(register_15_q),
    .in14(register_14_q), .in15(register_13_q), .in16(register_17_q), .in17(register_18_q),
    .in18(register_19_q), .in19(register_20_q), .in20(register_21_q), .in21(register_22_q),
    .in22(register_23_q), .in23(register_24_q), .in24(register_25_q), .in25(register_26_q),
    .in26(register_27_q), .in27(register_28_q), .in28(register_29_q), .in29(register_30_q),
    .in30(register_31_q), .in31(register_32_q), .out(out_8), .sel(RS));  // open: en
  Multiplexer #(.select(5), .width(32)) multiplexer_2 (
    .in0(register_1_q), .in1(register_2_q), .in2(register_3_q), .in3(register_4_q), .in4(register_5_q),
    .in5(register_6_q), .in6(register_7_q), .in7(register_8_q), .in8(register_9_q), .in9(register_10_q),
    .in10(register_11_q), .in11(register_12_q), .in12(register_13_q), .in13(register_14_q),
    .in14(register_15_q), .in15(register_16_q), .in16(register_17_q), .in17(register_18_q),
    .in18(register_19_q), .in19(register_20_q), .in20(register_21_q), .in21(register_22_q),
    .in22(register_23_q), .in23(register_24_q), .in24(register_25_q), .in25(register_26_q),
    .in26(register_27_q), .in27(register_28_q), .in28(register_29_q), .in29(register_30_q),
    .in30(register_31_q), .in31(register_32_q), .out(out_9), .sel(RT));  // open: en
  Demultiplexer #(.select(5)) demultiplexer_1 (
    .out0(demultiplexer_1_out0), .out1(demultiplexer_1_out1), .out2(demultiplexer_1_out2),
    .out3(demultiplexer_1_out3), .out4(demultiplexer_1_out4), .out5(demultiplexer_1_out5),
    .out6(demultiplexer_1_out6), .out7(demultiplexer_1_out7), .out8(demultiplexer_1_out8),
    .out9(demultiplexer_1_out9), .out10(demultiplexer_1_out10), .out11(demultiplexer_1_out11),
    .out12(demultiplexer_1_out12), .out13(demultiplexer_1_out13), .out14(demultiplexer_1_out14),
    .out15(demultiplexer_1_out15), .out16(demultiplexer_1_out16), .out17(demultiplexer_1_out17),
    .out18(demultiplexer_1_out18), .out19(demultiplexer_1_out19), .out20(demultiplexer_1_out20),
    .out21(demultiplexer_1_out21), .out22(demultiplexer_1_out22), .out23(demultiplexer_1_out23),
    .out24(demultiplexer_1_out24), .out25(demultiplexer_1_out25), .out26(demultiplexer_1_out26),
    .out27(demultiplexer_1_out27), .out28(demultiplexer_1_out28), .out29(demultiplexer_1_out29),
    .out30(demultiplexer_1_out30), .out31(demultiplexer_1_out31), .in(WE), .sel(RD));  // open: en
  Register #(.width(32)) register_13 (.D(WD), .en(demultiplexer_1_out12), .Q(register_13_q), .clk(clk), .clr(reset));
  Register #(.width(32)) register_14 (.D(WD), .en(demultiplexer_1_out13), .Q(register_14_q), .clk(clk), .clr(reset));
  Register #(.width(32)) register_15 (.D(WD), .en(demultiplexer_1_out14), .Q(register_15_q), .clk(clk), .clr(reset));
  Register #(.width(32)) register_16 (.D(WD), .en(demultiplexer_1_out15), .Q(register_16_q), .clk(clk), .clr(reset));
  Register #(.width(32)) register_17 (.D(WD), .en(demultiplexer_1_out16), .Q(register_17_q), .clk(clk), .clr(reset));
  Register #(.width(32)) register_18 (.D(WD), .en(demultiplexer_1_out17), .Q(register_18_q), .clk(clk), .clr(reset));
  Register #(.width(32)) register_19 (.D(WD), .en(demultiplexer_1_out18), .Q(register_19_q), .clk(clk), .clr(reset));
  Register #(.width(32)) register_20 (.D(WD), .en(demultiplexer_1_out19), .Q(register_20_q), .clk(clk), .clr(reset));
  Register #(.width(32)) register_21 (.D(WD), .en(demultiplexer_1_out20), .Q(register_21_q), .clk(clk), .clr(reset));
  Register #(.width(32)) register_22 (.D(WD), .en(demultiplexer_1_out21), .Q(register_22_q), .clk(clk), .clr(reset));
  Register #(.width(32)) register_23 (.D(WD), .en(demultiplexer_1_out22), .Q(register_23_q), .clk(clk), .clr(reset));
  Register #(.width(32)) register_24 (.D(WD), .en(demultiplexer_1_out23), .Q(register_24_q), .clk(clk), .clr(reset));
  Register #(.width(32)) register_25 (.D(WD), .en(demultiplexer_1_out24), .Q(register_25_q), .clk(clk), .clr(reset));
  Register #(.width(32)) register_26 (.D(WD), .en(demultiplexer_1_out25), .Q(register_26_q), .clk(clk), .clr(reset));
  Register #(.width(32)) register_27 (.D(WD), .en(demultiplexer_1_out26), .Q(register_27_q), .clk(clk), .clr(reset));
  Register #(.width(32)) register_28 (.D(WD), .en(demultiplexer_1_out27), .Q(register_28_q), .clk(clk), .clr(reset));
  Register #(.width(32)) register_29 (.D(WD), .en(demultiplexer_1_out28), .Q(register_29_q), .clk(clk), .clr(reset));
  Register #(.width(32)) register_30 (.D(WD), .en(demultiplexer_1_out29), .Q(register_30_q), .clk(clk), .clr(reset));
  Register #(.width(32)) register_31 (.D(WD), .en(demultiplexer_1_out30), .Q(register_31_q), .clk(clk), .clr(reset));
  Register #(.width(32)) register_32 (.D(WD), .en(demultiplexer_1_out31), .Q(register_32_q), .clk(clk), .clr(reset));

  // Other names for the same wires on the sheet: RST = reset
endmodule

module ALU (
  input  [31:0] opA,
  input  [31:0] opB,
  input  [1:0] ALUctr,
  output [31:0] ALUout,
  output zero
);

  wire [31:0] adder_1_out, or_1_out, subtractor_1_out;

  Adder #(.width(32)) adder_1 (.a(opA), .b(opB), .out(adder_1_out));  // open: cin, cout
  Subtractor #(.width(32)) subtractor_1 (.a(opA), .b(opB), .out(subtractor_1_out));  // open: bin, bout
  assign or_1_out = opA | opB;  // OR_Gate or_1, 32 bits wide
  Comparator #(.width(32), .mode("unsigned")) comparator_1 (.a(opA), .b(opB), .eq(zero));  // open: gt, lt
  Multiplexer #(.select(2), .width(32)) multiplexer_1 (
    .in0(adder_1_out), .in1(subtractor_1_out), .in2(or_1_out), .out(ALUout), .sel(ALUctr));  // open: in3, en
endmodule

module DM (
  input  [4:0] Addr,
  input  [31:0] data_w,
  input  write_en,
  input  clk,
  input  reset,
  output [31:0] data_r
);

  RAM #(.addrWidth(5), .dataWidth(32), .bus("separate")) ram_1 (
    .addr(Addr), .din(data_w), .data(data_r), .str(write_en), .clk(clk), .clr(reset));  // open: sel, ld
endmodule

module EXT (
  input  [15:0] in_1,
  input  [1:0] in_2,
  output [31:0] out_3
);

  wire [31:0] bit_extender_1_out, bit_extender_2_out;

  assign bit_extender_1_out = {{16{1'b0}}, in_1};  // Bit_Extender bit_extender_1
  assign bit_extender_2_out = {{16{in_1[15]}}, in_1};  // Bit_Extender bit_extender_2
  Multiplexer #(.select(2), .width(32)) multiplexer_1 (
    .in0(bit_extender_1_out), .in1(bit_extender_2_out), .in2({in_1, {16{1'b0}}}), .out(out_3), .sel(in_2));  // open: in3, en
endmodule

module Controller (
  input  [5:0] opcode,
  input  [5:0] func,
  output nPC_sel,
  output GRF_WE,
  output DM_WE,
  output GRF_WD,
  output ALUsrc,
  output GRF_WS,
  output [1:0] ALUctr,
  output [1:0] EXTctr
);

  wire addu, beq, lui, lw, nop, not_1_out, not_2_out, not_3_out, not_4_out, not_5_out, not_6_out, not_7_out,
       not_8_out, not_9_out, not_10_out, not_11_out, not_12_out, ori, rtype, subu, sw;

  not not_1 (not_1_out, opcode[5]);
  not not_2 (not_2_out, opcode[4]);
  not not_3 (not_3_out, opcode[3]);
  not not_4 (not_4_out, opcode[1]);
  not not_5 (not_5_out, opcode[2]);
  not not_6 (not_6_out, opcode[0]);
  and u_rtype (rtype, not_6_out, not_4_out, not_5_out, not_3_out, not_2_out, not_1_out);
  and u_ori (ori, opcode[0], not_4_out, opcode[2], opcode[3], not_2_out, not_1_out);
  and u_lw (lw, opcode[0], opcode[1], not_5_out, not_3_out, not_2_out, opcode[5]);
  and u_sw (sw, opcode[0], opcode[1], not_5_out, opcode[3], not_2_out, opcode[5]);
  and u_beq (beq, not_6_out, not_4_out, opcode[2], not_3_out, not_2_out, not_1_out);
  and u_lui (lui, opcode[0], opcode[1], opcode[2], opcode[3], not_2_out, not_1_out);
  not not_7 (not_7_out, func[5]);
  not not_8 (not_8_out, func[4]);
  not not_9 (not_9_out, func[3]);
  not not_10 (not_10_out, func[1]);
  not not_11 (not_11_out, func[2]);
  not not_12 (not_12_out, func[0]);
  and u_addu (addu, rtype, func[0], not_10_out, not_11_out, not_9_out, not_8_out, func[5]);
  and u_subu (subu, rtype, func[0], func[1], not_11_out, not_9_out, not_8_out, func[5]);
  and u_nop (nop, rtype, not_12_out, not_10_out, not_11_out, not_9_out, not_8_out, not_7_out);
  buf or_1 (nPC_sel, beq);  // OR_Gate
  or or_2 (GRF_WE, addu, subu, ori, lw, lui);
  buf or_3 (DM_WE, sw);  // OR_Gate
  or or_4 (ALUsrc, ori, lw, sw, lui);
  or or_5 (GRF_WD, addu, subu);
  buf or_6 (GRF_WS, lw);  // OR_Gate
  buf or_7 (ALUctr[1], ori);  // OR_Gate
  or or_8 (ALUctr[0], subu, beq);
  or or_9 (EXTctr[0], lw, sw);
  buf or_10 (EXTctr[1], lui);  // OR_Gate
endmodule
